# Fritzing sketch schematic (saved by Fritzing 0.7.12b)
breadboards: 1

parts:
  LCD1 = LCD screen
  Contrast = Trimmer Potentiometer [maximum_resistance=10kΩ package=THT]
  Atmega_328 = atmega328 [package=dip]
  16MHZ = Crystal [frequency="16 Mhz" package=THT]
  C1 = Ceramic Disk Capacitor [package=THT]
  C2 = Ceramic Disk Capacitor [package=THT]
  R2 = 1k Ω Resistor [package=THT]
  J2 = Generic female header - 2 pins [package=THT]
  +12 = Generic female header - 2 pins [package=THT]
  7805 = Voltage Regulator - 5V [package="TO220 [THT]"]
  Backlight = Trimmer Potentiometer [maximum_resistance=10kΩ package=THT]
  J5 = Generic female header [package=THT]
  J6 = Generic female header - metal rounded [package=THT]
  J7 = Generic female header - metal rounded [package=THT]
  Select_Fuel = Generic female header - 3 pins [package=THT]
  R5 = 1k Ω Resistor [package=THT]
  J9 = Generic female header - metal rounded [package=THT]
  J10 = Generic female header - metal rounded [package=THT]
  Q2 = NPN-Transistor [package="TO92 [THT]"]
  R6 = 470 Ω Resistor [package=THT]
  R7 = 470 Ω Resistor [package=THT]
  +13 = Generic female header - 2 pins [package=THT]

nets:
  VSS: LCD1.VSS, LCD1.R/W, LCD1.LED-, Contrast.leg2, Atmega_328.GND#7, C1.pin_0, C2.pin_0, +12.pin2, 7805.GND, Backlight.leg1, J7.pin1, R5.Pin_0, Q2.emitter
  VDD: LCD1.VDD, Contrast.leg1, Atmega_328.VCC, Atmega_328.AVCC, R2.Pin_0, 7805.output_voltage, Backlight.leg2, Select_Fuel.pin1, R7.Pin_0
  N1: LCD1.V0, Contrast.wiper
  N2: LCD1.RS, J9.pin1
  N3: LCD1.E, Atmega_328.D6_(PWM)
  N4: LCD1.DB4, Atmega_328.D5_(PWM)
  N5: LCD1.DB5, Atmega_328.D4
  N6: LCD1.DB6, Atmega_328.D3_(PWM)
  N7: LCD1.DB7, Atmega_328.D2
  N8: LCD1.LED+, Backlight.wiper
  N9: Atmega_328.RESET, R2.Pin_1
  N10: Atmega_328.D0_(RX), J2.pin2
  N11: Atmega_328.D1_(TX), J2.pin1
  N12: Atmega_328.XLAT1, 16MHZ.pin_1, C2.pin_1
  N13: Atmega_328.XLAT2, 16MHZ.pin_0, C1.pin_1
  N14: Atmega_328.D7, J5.pin1
  N15: Atmega_328.D9_(PWM), R6.Pin_1
  N16: Atmega_328.D10_(PWM), J10.pin1
  N17: Atmega_328.GND#21, J6.pin1
  N18: Atmega_328.A4, Select_Fuel.pin3
  N19: Atmega_328.A5, Select_Fuel.pin2, R5.Pin_1
  N20: +12.pin1, 7805.input_voltage
  N21: Q2.base, R6.Pin_0
  N22: R7.Pin_1, +13.pin2

notes:
  Megaviewer 0.1
